# Fritzing sketch Design (saved by Fritzing 0.9.2b)
circuit board: 11.8352cm x 6.6019cm

parts:
  DS1 = DS18B20 1-Wire Temperature Sensor [part_number=DS18B20]
  R1 = Resistor [tolerance=±5% resistance=220 package="2512 [SMD]"]
  U1 = LCD-16X2 [package=lcd-16x2_nosilk]
  R2 = Trimmer Potentiometer [maximum_resistance=10kΩ package=THT]
  ZS-042_RTC1 = ZS-042 RTC Module
  Part2 = MicroSD Card Module
  R3 = Resistor [tolerance=±5% resistance=220 package="2512 [SMD]"]
  Arduino1 = Arduino Mini (Rev5)

nets:
  GND: DS1.GND, U1.VSS, U1.R_W, U1.K, R2.leg2, ZS-042_RTC1.GND, Part2.GND, Arduino1.GND
  N1: DS1.DQ, R1.Pin_1, Arduino1.D6_PWM
  VDD: DS1.VDD, R1.Pin_0, U1.VDD, R2.leg1, ZS-042_RTC1.VCC, Part2.VCC, R3.Pin_1, Arduino1.5V
  N2: U1.VO, R2.wiper
  N3: U1.RS, Arduino1.D9_PWM
  N4: U1.E, Arduino1.D8
  N5: U1.DB4, Arduino1.D5_PWM
  N6: U1.DB5, Arduino1.D4
  N7: U1.DB6, Arduino1.D3_PWM
  N8: U1.DB7, Arduino1.D2
  N9: U1.A, R3.Pin_0
  N10: ZS-042_RTC1.SDA, Arduino1.A4
  N11: ZS-042_RTC1.SCL, Arduino1.A5
  N12: Part2.MISO, Arduino1.D11_PWM
  N13: Part2.MOSI, Arduino1.D10_PWM
  N14: Part2.SCK, Arduino1.D12
  N15: Part2.CS, Arduino1.D7
